# Fritzing sketch MeditationTimer (saved by Fritzing 0.9.2b)
breadboards: 1

parts:
  The_Arduino = Arduino Uno (Rev3)
  Long_On = Super Flux LED blue [color=Blue]
  Timer_Set = Super Flux LED blue [color=Blue]
  Buzzer_On = Super Flux LED blue [color=Blue]
  Timer_Begin_/_Off = SPST Switch [package=switch-spdt_kit]
  Timer_Long_/_Short = SPST Switch [package=switch-spdt_kit]
  Buzzer_On_/_Off = SPST Switch [package=switch-spdt_kit]
  Alarm_Buzzer = Piezo Speaker
  LED_Protector = Resistor [tolerance=±5% resistance=220 package=THT]
  LED_Protector_2 = Resistor [tolerance=±5% resistance=220 package=THT]
  LED_Protector_3 = Resistor [tolerance=±5% resistance=220 package=THT]

nets:
  N1: The_Arduino.A0, Timer_Begin_/_Off.O
  N2: The_Arduino.A3, Timer_Long_/_Short.O
  N3: The_Arduino.D9_PWM, LED_Protector_3.Pin_1
  N4: The_Arduino.D11_PWM/MOSI, LED_Protector_2.Pin_1
  N5: The_Arduino.GND, Long_On.cathode, Timer_Set.cathode, Buzzer_On.cathode, Timer_Begin_/_Off.S, Timer_Long_/_Short.S, Buzzer_On_/_Off.S, Alarm_Buzzer.pin2
  N6: The_Arduino.A5/SCL, Buzzer_On_/_Off.O
  N7: The_Arduino.D2, Alarm_Buzzer.pin1
  N8: The_Arduino.D5_PWM, LED_Protector.Pin_1
  N9: Long_On.anode, LED_Protector_3.Pin_0
  N10: Timer_Set.anode, LED_Protector.Pin_0
  N11: Buzzer_On.anode, LED_Protector_2.Pin_0
